# Fritzing sketch Pulsanti temporizzati (saved by Fritzing 0.9.3b)
breadboards: 1

parts:
  Componente1 = Arduino Uno (Rev3)
  LED2 = LED - 5mm [color="Red (633nm)" package="5 mm [THT]"]
  R1 = Resistor [tolerance=±5% resistance=220 package=THT]
  R2 = Resistor [tolerance=±5% resistance=220 package=THT]
  LED1 = LED - 5mm [color="Red (633nm)" package="5 mm [THT]"]
  R3 = Resistor [tolerance=±5% resistance=220 package=THT]
  S1 = Pushbutton [package="[THT]"]

nets:
  N1: Componente1.D12/MISO, R1.Pin_0
  N2: Componente1.D13/SCK, R2.Pin_0
  N3: Componente1.D2, R3.Pin_1, S1.Pin_3, S1.Pin_4
  N4: Componente1.5V, S1.Pin_1, S1.Pin_2
  N5: Componente1.GND, LED2.anode, LED1.anode, R3.Pin_0
  N6: LED2.cathode, R1.Pin_1
  N7: R2.Pin_1, LED1.cathode
